# Fritzing sketch Stromputer (saved by Fritzing 0.7.10b)

parts:
  LCD1 = LCD screen
  Rled1 = Resistor [tolerance=±5% resistance=1k package=THT]
  Nano1 = Arduino Nano v2.3
  LED1 = LED - 5mm [color="Green (570nm)" package="5 mm [THT]"]
  Rled2 = Resistor [tolerance=±5% resistance=1k package=THT]
  LED2 = LED - 5mm [color="Green (570nm)" package="5 mm [THT]"]
  Rled3 = Resistor [tolerance=±5% resistance=1k package=THT]
  LED3 = LED - 5mm [color="Yellow (595nm)" package="5 mm [THT]"]
  Rled4 = Resistor [tolerance=±5% resistance=1k package=THT]
  LED4 = LED - 5mm [color="Yellow (595nm)" package="5 mm [THT]"]
  Rled5 = Resistor [tolerance=±5% resistance=1k package=THT]
  LED5 = LED - 5mm [color="White (4500K)" package="5 mm [THT]"]
  Rled6 = Resistor [tolerance=±5% resistance=1k package=THT]
  LED6 = LED - 5mm [color="Blue (525nm)" package="5 mm [THT]"]
  CdS = Photocell (LDR) [package=THT]
  Rcds = Resistor [tolerance=±5% resistance=220 package=THT]
  DC_Power1 = DC Power [voltage=12]
  Rbatt2 = Resistor [tolerance=±5% resistance=220 package=THT]
  Rbatt1 = Resistor [tolerance=±5% resistance=220 package=THT]
  Rgps1 = Resistor [tolerance=±0.05% resistance=965M package=THT]
  Rgps2 = Resistor [tolerance=±0.05% resistance=965M package=THT]
  LM2940 = Voltage Regulator - 5V [package="TO220 [THT]"]
  D1 = Zener Diode [part_number=1N4732A breakdown_voltage=3.6V package="300 mil [THT]"]
  Cin1 = Electrolytic Capacitor [capacitance=220µF package="100 mil [THT, electrolytic]"]
  Cout = Electrolytic Capacitor [capacitance=22µF package="100 mil [THT, electrolytic]"]
  U6 = mystery part, 3 pins [chip_label=DS18B20 spacing=300mil part_number=DS1820]
  Ronewire = Resistor [tolerance=±5% resistance=220 package=THT]
  Cin2 = Electrolytic Capacitor [capacitance=0.47µF package="100 mil [THT, electrolytic]"]
  Rin = Resistor [tolerance=±5% resistance=16 power=3W package=THT]
  V-STROM_GPS = Rotary Potentiometer (Small) [maximum_resistance=100kΩ]
  DC_Power2 = DC Power [voltage=5]

nets:
  GND: LCD1.VSS, Nano1.GND, LED1.cathode, LED2.cathode, LED3.cathode, LED4.cathode, LED5.cathode, LED6.cathode, Rcds.Pin_1, DC_Power1.GND, Rbatt2.Pin_1, Rgps2.Pin_1, LM2940.GND, D1.anode, Cin1.-, Cout.-, U6.pin1, Cin2.-, V-STROM_GPS.leg1, DC_Power2.GND
  VDD: LCD1.VDD, Nano1.+5V, CdS.pin_0, LM2940.output_voltage, Cout.+, U6.pin3, Ronewire.Pin_1
  N1: LCD1.DB0, Nano1.D1TX
  N2: LCD1.DB1, Nano1.D0RX
  N3: Rled1.Pin_0, Nano1.D3
  N4: Rled1.Pin_1, LED1.anode
  N5: Nano1.D4, U6.pin2, Ronewire.Pin_0
  N6: Nano1.D5, Rled2.Pin_0
  N7: Nano1.D6, Rled3.Pin_0
  N8: Nano1.D9, Rled4.Pin_0
  N9: Nano1.D10, Rled5.Pin_0
  N10: Nano1.D11, Rled6.Pin_0
  N11: Nano1.A3, Rgps1.Pin_1, Rgps2.Pin_0
  N12: Nano1.A2, CdS.pin_1, Rcds.Pin_0
  N13: Nano1.A0, Rbatt2.Pin_0, Rbatt1.Pin_1
  N14: Rled2.Pin_1, LED2.anode
  N15: Rled3.Pin_1, LED3.anode
  N16: Rled4.Pin_1, LED4.anode
  N17: Rled5.Pin_1, LED5.anode
  N18: Rled6.Pin_1, LED6.anode
  N19: DC_Power1.V+, Rbatt1.Pin_0, Rin.Pin_1
  N20: Rgps1.Pin_0, V-STROM_GPS.wiper
  N21: LM2940.input_voltage, D1.cathode, Cin1.+, Cin2.+, Rin.Pin_0
  N22: V-STROM_GPS.leg2, DC_Power2.V+

notes:
  I2C
  LCD I2C ports may be already pulled up internally
  12V BATT
  GPS - Gear Position Level sensor
  (0..5V)
  Pink wire
  Stromputer, Stromputer - A motorcycle computer and display for V-Strom computers, 2.0
  7805=LM2940 5V
  One wire
  5V ECU
