# Fritzing sketch Mk1B Prototype V0.7 (saved by Fritzing 0.6.3b)
breadboards: 1

parts:
  R1 = Resistor [tolerance=±5% resistance=220 package=THT]
  LED1 = LED - 5mm [color="Yellow (595nm)" package="5 mm [THT]"]
  DC_Power2 = DC Power [voltage=5]
  Arduino1 = Arduino
  IC1 = IC, DIP package, 8 pins [chip_label=DS1631 spacing=300mil]
  LCD1 = LCD screen
  IC2 = IC, DIP package, 14 pins [chip_label=PCF8591 spacing=300mil]
  R2 = Resistor [tolerance=±5% resistance=33k package=THT]
  R4 = 220___Resistor
  R5 = Resistor [tolerance=±5% resistance=68k package=THT]
  R6 = Resistor [tolerance=±5% resistance=68k package=THT]
  R7 = Resistor [tolerance=±5% resistance=1.5k package=THT]
  R8 = Resistor [tolerance=±5% resistance=1.5k package=THT]

nets:
  N1: R1.Pin_1, LED1.anode, DC_Power2.V+, IC1.pin8, R7.Pin_1, R8.Pin_1
  GND: DC_Power2.GND, Arduino1.GND, IC1.pin4, IC1.pin5, IC1.pin6, IC1.pin7, R2.Pin_0, R5.Pin_0
  N2: Arduino1.A4, IC1.pin1, R8.Pin_0
  N3: Arduino1.A5, IC1.pin2, R7.Pin_0
  N4: LCD1.DB0, LCD1.DB3
  N5: IC2.pin10, R2.Pin_1, R4.connector0
  N6: IC2.pin11, R5.Pin_1, R6.Pin_0

notes:
  I2C
  SDA - Blue
  SCL - Yellow
  Batt Volt Div 1:4
  33K:139K
  Gear Position Volt Div 1:2
  68K:68K
  I2C
  Pull Up
  Resistors
  1.5K
  MC 12V Batt
  MC Gear Position Sensor (PosiTap to Pink Wire)
  Mk1B Prototype
